// Logisim project circuit_diagram.circ as structural Verilog
module FskyFsescMiniV6dot7Pro (
  input  in_1,
  input  in_2,
  output comm_5v,
  output comm_3dot3v,
  output comm_negative,
  output comm_ADC1,
  output comm_RX_or_SDA,
  output comm_TX_or_SCL,
  output comm_ADC2,
  output comm_ADC3,
  output swd_3dot3v,
  output swd_swclk,
  output swd_negative,
  output swd_swdio,
  output swd_nrst,
  output A,
  output B,
  output C,
  output receiver_negative,
  output receiver_5v,
  output receiver_signal,
  output sense_5v,
  output sense_tmp,
  output sense_H1,
  output sense_H2,
  output sense_H3,
  output sense_NEGATIVE,
  output usb_5v_negative,
  output usb_data_plus,
  output usb_data_minus,
  output usb_5v_positive,
  output can_5v,
  output can_CAH,
  output can_CAL,
  output can_NEGATIVE
);
endmodule
